# Fritzing sketch fritzing (saved by Fritzing 0.9.2b)
breadboards: 1

parts:
  U1_TSOP4838 = IR Receiver Breakout [package=PCB]
  C1 = Ceramic Capacitor [capacitance=100nF package="100 mil [THT, multilayer]"]
  C2 = Ceramic Capacitor [capacitance=100nF package="100 mil [THT, multilayer]"]
  U1_ATtiny45 = ATTINY45 [package=dip]
  R1 = Resistor [tolerance=±5% resistance=100 package=THT]
  Q1 = PNP-Transistor [package="TO92 [THT]"]
  R2 = Resistor [tolerance=±5% resistance=330 package=THT]
  LED1 = LED - 5mm [color="Green (570nm)" package="5 mm [THT]"]
  LED2 = LED - 5mm [color="Red (633nm)" package="5 mm [THT]"]
  R4 = Trimmer Potentiometer [maximum_resistance=250kΩ package=THT]
  R5 = Resistor [tolerance=±5% resistance=330 package=THT]
  R6 = Resistor [tolerance=±5% resistance=100k package=THT]
  R7 = Resistor [tolerance=±5% resistance=100k package=THT]

nets:
  GND: U1_TSOP4838.GND, C1.0, C2.0, U1_ATtiny45.GND, R2.Pin_1, R4.leg1, R5.Pin_0
  N1: U1_TSOP4838.OUT, U1_ATtiny45.PB1(MISO), Q1.B
  N2: U1_TSOP4838.VCC, C2.1, R1.Pin_0
  5V: C1.1, U1_ATtiny45.VCC, R1.Pin_1, LED1.anode, R6.Pin_0
  N3: U1_ATtiny45.PB0(MOSI), LED2.anode
  N4: U1_ATtiny45.PB2(SCK_ADC1), R7.Pin_0
  N5: Q1.E, LED1.cathode
  N6: Q1.C, R2.Pin_0
  N7: LED2.cathode, R5.Pin_1
  N8: R4.wiper, R7.Pin_1
  N9: R4.leg2, R6.Pin_1
